# Fritzing sketch current_connection (saved by Fritzing 0.9.5d)
stripboards: 1

parts:
  Part1 = Arduino Nano (Rev3.0)
  GLCD_128x1 = 128 x 64 Graphic LCD
  J1 = female pin header, 3 pins [form="♀ (female)"]
  J2 = female pin header, 3 pins [form="♀ (female)"]
  J3 = female pin header, 4 pins [form="♀ (female)"]
  J4 = female pin header, 4 pins [form="♀ (female)"]
  J5 = female pin header, 3 pins [form="♀ (female)"]
  J6 = female pin header, 3 pins [form="♀ (female)"]
  J7 = female pin header, 4 pins [form="♀ (female)"]
  J8 = female pin header, 4 pins [form="♀ (female)"]
  R1 = Resistor [tolerance=±5% resistance=3700 package=THT]
  J9 = female pin header, 6 pins [form="♀ (female)"]
  J10 = male pin header, 7 pins [form="♂ (male)"]
  J11 = male pin header, 7 pins [form="♂ (male)"]
  J12 = male pin header, 7 pins [form="♂ (male)"]
  J13 = male pin header, 7 pins [form="♂ (male)"]
  J14 = female pin header, 2 pins [form="♀ (female)"]

nets:
  N1: Part1.D2, GLCD_128x1.7_DB0, J4.pin4, J7.pin4
  N2: Part1.D3, GLCD_128x1.8_DB1, J4.pin3, J7.pin3
  N3: Part1.D4, GLCD_128x1.9_BD2, J4.pin2, J7.pin2
  N4: Part1.D5, GLCD_128x1.10_DB3, J4.pin1, J7.pin1
  N5: Part1.D6, GLCD_128x1.11_DB4, J3.pin4, J8.pin4
  N6: Part1.D7, GLCD_128x1.12_DB5, J3.pin3, J8.pin3
  N7: Part1.D8, GLCD_128x1.13_DB6, J3.pin2, J8.pin2
  N8: Part1.D9, GLCD_128x1.14_DB7, J3.pin1, J8.pin1
  N9: Part1.D10, GLCD_128x1.15_CS1, J2.pin3, J5.pin3
  N10: Part1.D11/MOSI, GLCD_128x1.16_CS2, J2.pin2, J5.pin2
  N11: Part1.D12/MISO, GLCD_128x1.17_RST, J2.pin1, J5.pin1
  N12: Part1.A2, GLCD_128x1.4_D/I, J1.pin3, J6.pin3
  N13: Part1.A1, GLCD_128x1.5_R/W, J1.pin2, J6.pin2
  N14: Part1.A0, GLCD_128x1.6_Enable, J1.pin1, J6.pin1
  N15: GLCD_128x1.1_Vss, J9.pin3, J10.pin4, J11.pin4, J12.pin4, J13.pin4
  N16: GLCD_128x1.2_Vdd, J9.pin4, J10.pin5, J11.pin5, J12.pin5, J13.pin5
  N17: GLCD_128x1.3_Vo, R1.Pin_0
  N18: GLCD_128x1.18_Vout, R1.Pin_1
  N19: GLCD_128x1.19_A(+), J9.pin1, J10.pin2, J11.pin2, J12.pin2, J13.pin2
  N20: GLCD_128x1.20_K(-), J9.pin2, J10.pin3, J11.pin3, J12.pin3, J13.pin3
  N21: J9.pin5, J10.pin6, J11.pin6, J12.pin6, J13.pin6, J14.pin2
  N22: J9.pin6, J10.pin7, J11.pin7, J12.pin7, J13.pin7, J14.pin1
  N23: J10.pin1, J11.pin1, J12.pin1, J13.pin1

notes:
  SDA
  SCL
  VCC
  GND
